# Fritzing sketch LatencyProbe (saved by Fritzing 0.9.2b)
breadboards: 1

parts:
  Bauteil1 = Arduino Nano (Rev3.0)
  R1 = Photocell (LDR) [package=THT]
  C1 = Ceramic Capacitor [capacitance=100nF package="100 mil [THT, multilayer]"]
  R1_-_10kOhm1 = Resistor [tolerance=±1% resistance=330 package=THT]
  LED1 = LED - 5mm [color="Blue (430nm)" package="5 mm [THT]"]
  R1_-_10kOhm2 = Resistor [tolerance=±1% resistance=330 package=THT]
  Q1 = PNP-Transistor [package="TO92 [THT]"]
  C2 = Electrolytic Capacitor [capacitance=10µF voltage=250V package="100 mil [THT, electrolytic]"]
  Pro_Micro1 = Pro Micro
  LED2 = LED - 5mm [color="Green (555nm)" package="5 mm [THT]"]
  R1_-_10kOhm3 = Resistor [tolerance=±20% resistance=330 package=THT]
  S1 = Pushbutton [package="[THT]"]
  LED3 = LED - 5mm [color="Red (633nm)" package="5 mm [THT]"]
  U1 = mystery part, 20 pins [chip_label="Adafruit 2.8'' TFT LCD Breakout Board+"]
  R2 = Resistor [tolerance=±1% resistance=10k package=THT]
  R4 = Resistor [tolerance=±1% resistance=10k package=THT]
  R3 = Resistor [tolerance=±1% resistance=10k package=THT]
  U3 = RELAY [package=relay-jzc]
  D2 = Diode [package=diode-1n4148]

nets:
  N1: Bauteil1.GND, C1.1, R1_-_10kOhm1.Pin_0, C2.+, U1.pin1, R2.Pin_0, R4.Pin_1, R3.Pin_1, U3.MAIN, U3.COIL1, D2.A
  N2: Bauteil1.5V, R1.pin_0, C1.0, Q1.E, C2.-, R1_-_10kOhm3.Pin_1, S1.Pin_1, S1.Pin_2, LED3.anode, U1.pin2
  N3: Bauteil1.D13/SCK, Pro_Micro1.D7, S1.Pin_3, S1.Pin_4, R4.Pin_0
  N4: R1_-_10kOhm1.Pin_1, LED1.cathode
  N5: LED1.anode, Pro_Micro1.D20/A2
  N6: R1_-_10kOhm2.Pin_1, Q1.B
  N7: Q1.C, U3.NO, D2.C
  N8: Pro_Micro1.D9, U1.pin8
  N9: Pro_Micro1.D10, U1.pin7
  N10: Pro_Micro1.D16/MOSI, U1.pin6
  N11: Pro_Micro1.D14/MISO, U1.pin5
  N12: Pro_Micro1.D15/SCLK, U1.pin4
  N13: LED2.cathode, U3.COIL2
  N14: LED2.anode, R1_-_10kOhm3.Pin_0
  N15: LED3.cathode, R3.Pin_0

notes:
  JZC-11F
  actually
  connect green wire for
  automatic testing
  connect to soldered coin
  or capacitive sponge
  fixate on screen
  connect to
  (gaming) computer
  connect to display on pins for:
  CLK, MISO, MOSI, CS, D/C

custom parts:
  Pro Micro: The SparkFun Pro Micro is a complete USB-based microcontoller development system, in a very small footprint, capable of implementing many types of projects. All programming can be done via the USB port.
